// Logisim project Proyecto_final.circ as structural Verilog: 8 circuits, main circuit Juego Dinosaurio
module Juego_Dinosaurio (
  input  in_1,
  input  in_2,
  input  in_3,
  input  in_4
);

  wire _301, _302, _303, _304, _305, _306, _307, _308, _309, _311, _312, _313, _314, _315, _316, _317, _318,
       _319, _3010, _3011, _3012, _3013, _3014, _3015, _3110, _3111, _3112, _3113, _3114, _3115, a1, a2, a3,
       a4, a5, a6, a7, a8, agachar, and_2_out, and_3_out, and_4_out, and_5_out, and_6_out, and_7_out,
       and_8_out, b2, b3, b4, b5, b6, b7, b8, c1, c2, c3, c4, c5, c6, c7, c8, c9, c10, c11, c12, c13, c14,
       c15, c16, c17, c18, c19, c20, c21, c22, c23, c24, c25, c26, c27, c28, c29, c30, c31, c32, ca1, ca2,
       ca3, ca4, ca5, ca6, ca7, ce1, ce2, ce3, ce4, ce5, ce6, ce7, ch1, ch2, ch3, ch4, ci1, ci2, ci3, ci4,
       ci5, ci6, ci7, clk, clock_1_out, co1, co2, co3, co4, co5, co6, co7, comparator_2_eq, comparator_2_gt,
       comparator_3_eq, comparator_3_lt, d_ff_3_qn, d_ff_5_qn, d_ff_12_qn, d_ff_13_q, d_ff_16_qn, d_ff_17_qn,
       d_ff_25_qn, d_ff_28_qn, d_ff_29_qn, d_ff_37_qn, d_ff_38_qn, d_ff_43_qn, d_ff_44_qn, d_ff_45_qn,
       d_ff_54_qn, d_ff_55_qn, d_ff_56_qn, d_ff_63_qn, d_ff_64_q, d_ff_65_qn, d_ff_66_qn, d_ff_75_qn,
       d_ff_76_qn, dir2, dir3, dx, estado1, estado2, estado3, fin, Ini, Iniciar, k1, k2, k3, k4, k5,
       not_1_out, not_2_out, not_3_out, not_4_out, not_5_out, o1p, o2p, on, or_3_out, or_6_out, or_9_out,
       or_10_out, or_13_out, or_16_out, or_17_out, or_26_out, or_40_out, or_41_out, or_42_out, or_43_out,
       or_45_out, p1, p2, p3, p4, p5, p6, p7, q2, q3, q4, q5, s2, s3, s4, s5, s6, s7, s8, s9, s10, s11, s12,
       s13, s14, s15, s16, s17, s18, s19, s20, s21, s22, s23, s24, s25, s26, s27, s28, s29, s30, s31, s32,
       s33, saltar, sw, sw2;
  wire [1:0] random_1_out;
  wire [6:0] keyboard_1_data;

  Clock clock_1 (.out(clock_1_out));
  not not_1 (not_1_out, fin);
  D_Flip_Flop d_ff_1 (.clk(clk), .D(estado1), .Q(s2), .preset(estado1));  // open: Qn, en, reset
  D_Flip_Flop d_ff_2 (.clk(clk), .D(s13), .Q(s14));  // open: Qn, preset, en, reset
  D_Flip_Flop d_ff_3 (.clk(clk), .D(s25), .Q(s26), .Qn(d_ff_3_qn));  // open: preset, en, reset
  and and_1 (clk, clock_1_out, Ini, not_1_out);
  or or_1 (_3015, c31, p7);
  or or_2 (_3115, c32, p7);
  D_Flip_Flop d_ff_4 (.clk(clk), .D(s2), .Q(s3));  // open: Qn, preset, en, reset
  D_Flip_Flop d_ff_5 (.clk(clk), .D(s14), .Q(s15), .Qn(d_ff_5_qn));  // open: preset, en, reset
  D_Flip_Flop d_ff_6 (.clk(clk), .D(s26), .Q(s27));  // open: Qn, preset, en, reset
  D_Flip_Flop d_ff_7 (.clk(clk), .D(s3), .Q(s4));  // open: Qn, preset, en, reset
  D_Flip_Flop d_ff_8 (.clk(clk), .D(s15), .Q(s16));  // open: Qn, preset, en, reset
  D_Flip_Flop d_ff_9 (.clk(clk), .D(s27), .Q(s28));  // open: Qn, preset, en, reset
  and and_2 (and_2_out, saltar, not_2_out, dx);
  not not_2 (not_2_out, a1);
  or or_3 (or_3_out, a3, b5);
  or or_4 (_3014, p6, c31, p7);
  or or_5 (_3114, p6, c32, p7);
  D_Flip_Flop d_ff_10 (.clk(clk), .D(s4), .Q(s5));  // open: Qn, preset, en, reset
  D_Flip_Flop d_ff_11 (.clk(clk), .D(s16), .Q(s17));  // open: Qn, preset, en, reset
  D_Flip_Flop d_ff_12 (.clk(clk), .D(s28), .Q(s29), .Qn(d_ff_12_qn));  // open: preset, en, reset
  D_Flip_Flop d_ff_13 (.clk(clk), .D(and_2_out), .Q(d_ff_13_q), .preset(and_2_out), .reset(sw));  // open: Qn, en
  Demultiplexer #(.enable("false")) demultiplexer_1 (.out0(a1), .in(d_ff_13_q), .sel(dir2));  // open: out1
  Demultiplexer #(.enable("false")) demultiplexer_2 (.out0(a4), .out1(b4), .in(p3), .sel(dir2));
  D_Flip_Flop d_ff_14 (.clk(clk), .D(or_3_out), .Q(p3));  // open: Qn, preset, en, reset
  D_Flip_Flop d_ff_15 (.clk(clk), .D(or_6_out), .Q(p6));  // open: Qn, preset, en, reset
  or or_6 (or_6_out, a6, b8);
  or or_7 (_3013, p6, c31, p7, p5);
  or or_8 (_3113, p6, p7, c32, p5);
  D_Flip_Flop d_ff_16 (.clk(clk), .D(s5), .Q(s6), .Qn(d_ff_16_qn));  // open: preset, en, reset
  D_Flip_Flop d_ff_17 (.clk(clk), .D(s17), .Q(s18), .Qn(d_ff_17_qn));  // open: preset, en, reset
  D_Flip_Flop d_ff_18 (.clk(clk), .D(s29), .Q(s30));  // open: Qn, preset, en, reset
  Demultiplexer #(.enable("false")) demultiplexer_3 (.out0(a7), .out1(b7), .in(p6), .sel(dir2));
  D_Flip_Flop d_ff_19 (.clk(clk), .D(s6), .Q(s7));  // open: Qn, preset, en, reset
  D_Flip_Flop d_ff_20 (.clk(clk), .D(s18), .Q(s19));  // open: Qn, preset, en, reset
  D_Flip_Flop d_ff_21 (.clk(clk), .D(s30), .Q(s31));  // open: Qn, preset, en, reset
  D_Flip_Flop d_ff_22 (.clk(clk), .D(or_9_out), .Q(p1));  // open: Qn, preset, en, reset
  or or_9 (or_9_out, a1, b3);
  or or_10 (or_10_out, a4, b6);
  or or_11 (_3012, p4, p6, c31, p7, p5);
  or or_12 (_3112, p4, p7, c32, p6, p5);
  D_Flip_Flop d_ff_23 (.clk(clk), .D(s7), .Q(s8));  // open: Qn, preset, en, reset
  D_Flip_Flop d_ff_24 (.clk(clk), .D(s19), .Q(s20));  // open: Qn, preset, en, reset
  D_Flip_Flop d_ff_25 (.clk(clk), .D(s31), .Q(s32), .Qn(d_ff_25_qn));  // open: preset, en, reset
  Demultiplexer #(.enable("false")) demultiplexer_4 (.out0(a2), .out1(b2), .in(p1), .sel(dir2));
  Demultiplexer #(.enable("false")) demultiplexer_5 (.out0(a5), .out1(b5), .in(p4), .sel(dir2));
  D_Flip_Flop d_ff_26 (.clk(clk), .D(or_10_out), .Q(p4));  // open: Qn, preset, en, reset
  D_Flip_Flop d_ff_27 (.clk(clk), .D(or_13_out), .Q(p7));  // open: Qn, preset, en, reset
  or or_13 (or_13_out, a7, in_4);
  D_Flip_Flop d_ff_28 (.clk(clk), .D(s8), .Q(s9), .Qn(d_ff_28_qn));  // open: preset, en, reset
  D_Flip_Flop d_ff_29 (.clk(clk), .D(s20), .Q(s21), .Qn(d_ff_29_qn));  // open: preset, en, reset
  D_Flip_Flop d_ff_30 (.clk(clk), .D(s32), .Q(s33));  // open: Qn, preset, en, reset
  Comparator #(.width(1)) comparator_1 (.a(b2), .b(p1), .lt(sw));  // open: gt, eq
  Demultiplexer #(.enable("false")) demultiplexer_6 (.out0(a8), .out1(b8), .in(p7), .sel(dir2));
  or or_14 (_3011, p4, p5, p7, c31, p6, p3);
  or or_15 (_3111, p4, p5, p7, c32, p6, p3);
  D_Flip_Flop d_ff_31 (.clk(clk), .D(s9), .Q(s10));  // open: Qn, preset, en, reset
  D_Flip_Flop d_ff_32 (.clk(clk), .D(s21), .Q(s22));  // open: Qn, preset, en, reset
  D_Flip_Flop d_ff_33 (.clk(clk), .D(or_16_out), .Q(p2));  // open: Qn, preset, en, reset
  or or_16 (or_16_out, a2, b4);
  D_Flip_Flop d_ff_34 (.clk(clk), .D(or_17_out), .Q(p5));  // open: Qn, preset, en, reset
  or or_17 (or_17_out, a5, b7);
  or or_18 (_3010, p2, p4, p6, c31, p7, p5, p3);
  or or_19 (_3110, p2, p4, p7, c32, p6, p5, p3);
  T_Flip_Flop t_ff_1 (.Q(dir2), .preset(p7), .reset(sw));  // open: clk, T, Qn, en
  Demultiplexer #(.enable("false")) demultiplexer_7 (.out0(a3), .out1(b3), .in(p2), .sel(dir2));
  Demultiplexer #(.enable("false")) demultiplexer_8 (.out0(a6), .out1(b6), .in(p5), .sel(dir2));
  D_Flip_Flop d_ff_35 (.clk(clk), .D(s10), .Q(s11));  // open: Qn, preset, en, reset
  D_Flip_Flop d_ff_36 (.clk(clk), .D(s22), .Q(s23));  // open: Qn, preset, en, reset
  or or_20 (_309, p7, p2, p4, c31, p6, p5, p3, p1);
  or or_21 (_319, p3, p4, p6, c32, p7, p5, p2, p1);
  D_Flip_Flop d_ff_37 (.clk(clk), .D(s11), .Q(s12), .Qn(d_ff_37_qn));  // open: preset, en, reset
  D_Flip_Flop d_ff_38 (.clk(clk), .D(s23), .Q(s24), .Qn(d_ff_38_qn));  // open: preset, en, reset
  DotMatrix #(.inputtype("row"), .matrixcols(32), .matrixrows(16)) dotmatrix_1 (
    .row0({c32, c31, c30, c29, c28, c27, c26, c25, c24, c23, c22, c21, c20, c19, c18, c17, c16, c15, c14, c13, c12, c11, c10, c9, c8, c7, c6, c5, c4, c3, c2, c1}),
    .row1({_3115, _3015, c30, c29, c28, c27, c26, c25, c24, c23, c22, c21, c20, c19, c18, c17, c16, c15, c14, c13, c12, c11, c10, c9, c8, c7, c6, c5, c4, c3, c2, c1}),
    .row2({_3114, _3014, c30, c29, c28, c27, c26, c25, c24, c23, c22, c21, c20, c19, c18, c17, c16, c15, c14, c13, c12, c11, c10, c9, c8, c7, c6, c5, c4, c3, c2, c1}),
    .row3({_3113, _3013, c30, c29, c28, c27, c26, c25, c24, c23, c22, c21, c20, c19, c18, c17, c16, c15, c14, c13, c12, c11, c10, c9, c8, c7, c6, c5, c4, c3, c2, c1}),
    .row4({_3112, _3012, c30, c29, c28, c27, c26, c25, c24, c23, c22, c21, c20, c19, c18, c17, c16, c15, c14, c13, c12, c11, c10, c9, c8, c7, c6, c5, c4, c3, c2, c1}),
    .row5({_3111, _3011, c30, c29, c28, c27, c26, c25, c24, c23, c22, c21, c20, c19, c18, c17, c16, c15, c14, c13, c12, c11, c10, c9, c8, c7, c6, c5, c4, c3, c2, c1}),
    .row6({_3110, _3010, c30, c29, c28, c27, c26, c25, c24, c23, c22, c21, c20, c19, c18, c17, c16, c15, c14, c13, c12, c11, c10, c9, c8, c7, c6, c5, c4, c3, c2, c1}),
    .row7({_319, _309, c30, c29, c28, c27, c26, c25, c24, c23, c22, c21, c20, c19, c18, c17, c16, c15, c14, c13, c12, c11, c10, c9, c8, c7, c6, c5, c4, c3, c2, c1}),
    .row8({_318, _308, c30, c29, c28, c27, c26, c25, c24, c23, c22, c21, c20, c19, c18, c17, c16, c15, c14, c13, c12, c11, c10, c9, c8, c7, c6, c5, c4, c3, c2, c1}),
    .row9({_317, _307, c30, c29, c28, c27, c26, c25, c24, c23, c22, c21, c20, c19, c18, c17, c16, c15, c14, c13, c12, c11, c10, c9, c8, c7, c6, c5, c4, c3, c2, c1}),
    .row10({_316, _306, {30{1'b0}}}),
    .row11({_315, _305, s31, s30, s29, s28, s27, s26, s25, s24, s23, s22, s21, s20, s19, s18, s17, s16, s15, s14, s13, s12, s11, s10, s9, s8, s7, s6, s5, s4, s3, s2}),
    .row12({_314, _304, s31, s30, s29, s28, s27, s26, s25, s24, s23, s22, s21, s20, s19, s18, s17, s16, s15, s14, s13, s12, s11, s10, s9, s8, s7, s6, s5, s4, s3, s2}),
    .row13({_313, _303, s31, s30, s29, s28, s27, s26, s25, s24, s23, s22, s21, s20, s19, s18, s17, s16, s15, s14, s13, s12, s11, s10, s9, s8, s7, s6, s5, s4, s3, s2}),
    .row14({_312, _302, s31, s30, s29, s28, s27, s26, s25, s24, s23, s22, s21, s20, s19, s18, s17, s16, s15, s14, s13, s12, s11, s10, s9, s8, s7, s6, s5, s4, s3, s2}),
    .row15({_311, _301, s31, s30, s29, s28, s27, s26, s25, s24, s23, s22, s21, s20, s19, s18, s17, s16, s15, s14, s13, s12, s11, s10, s9, s8, s7, s6, s5, s4, s3, s2}));
  or or_22 (_308, dx, s32, p4, p5, c31, p7, p6, p3, p2, p1);
  or or_23 (_318, dx, p2, p4, p6, c32, p7, p5, p3, s33, p1);
  D_Flip_Flop d_ff_39 (.clk(clk), .D(s12), .Q(s13));  // open: Qn, preset, en, reset
  D_Flip_Flop d_ff_40 (.clk(clk), .D(s24), .Q(s25));  // open: Qn, preset, en, reset
  and and_3 (and_3_out, c14, c15);
  and and_4 (and_4_out, s15, s16);
  or or_24 (_307, dx, c31, p3, p5, ch1, p6, p4, p2, p1);
  or or_25 (_317, dx, p2, p4, p6, ch1, p5, p3, c32, p1);
  or or_26 (or_26_out, and_3_out, estado3, and_4_out);
  or or_27 (_306, dx, ch1, p3, p5, ch2, p4, p2, p1);
  or or_28 (_316, dx, p2, p3, p5, ch2, p4, ch1, p1);
  D_Flip_Flop d_ff_41 (.clk(clk), .D(estado2), .Q(c1), .preset(estado2));  // open: Qn, en, reset
  D_Flip_Flop d_ff_42 (.clk(clk), .D(c12), .Q(c13));  // open: Qn, preset, en, reset
  D_Flip_Flop d_ff_43 (.clk(clk), .D(c24), .Q(c25), .Qn(d_ff_43_qn));  // open: preset, en, reset
  Random #(.width(2), .trigger("falling")) random_1 (.clk(clk), .next(or_26_out), .out(random_1_out));  // open: clr
  or or_29 (_305, ch2, dx, s32, p4, ch1, p3, p2, p1, ch3);
  or or_30 (_315, ch3, p4, dx, p2, ch1, p3, s33, p1, ch2);
  D_Flip_Flop d_ff_44 (.clk(clk), .D(c1), .Q(c2), .Qn(d_ff_44_qn));  // open: preset, en, reset
  D_Flip_Flop d_ff_45 (.clk(clk), .D(c13), .Q(c14), .Qn(d_ff_45_qn));  // open: preset, en, reset
  D_Flip_Flop d_ff_46 (.clk(clk), .D(c25), .Q(c26));  // open: Qn, preset, en, reset
  _7_Segment_Display u_7_segment_display_1 (.g(ce7), .f(ce6), .a(ce1), .b(ce2), .e(ce5), .d(ce4), .c(ce3));  // open: dp
  _7_Segment_Display u_7_segment_display_2 (.g(ci7), .f(ci6), .a(ci1), .b(ci2), .e(ci5), .d(ci4), .c(ci3));  // open: dp
  Button Iniciar_Juego (.out(Iniciar));
  _7_Segment_Display u_7_segment_display_3 (.g(ca7), .f(ca6), .a(ca1), .b(ca2), .e(ca5), .d(ca4), .c(ca3));  // open: dp
  _7_Segment_Display u_7_segment_display_4 (.g(co7), .f(co6), .a(co1), .b(co2), .e(co5), .d(co4), .c(co3));  // open: dp
  and and_5 (and_5_out, o1p, o2p, comparator_2_eq);
  Comparator #(.width(2), .mode("unsigned")) comparator_2 (
    .a(2'b01), .b(random_1_out), .gt(comparator_2_gt), .eq(comparator_2_eq));  // open: lt
  Comparator #(.width(2), .mode("unsigned")) comparator_3 (
    .a(2'b10), .b(random_1_out), .eq(comparator_3_eq), .lt(comparator_3_lt));  // open: gt
  or or_31 (_304, dx, s32, p3, on, p2, p1);
  or or_32 (_314, dx, p2, p3, s33, on, p1);
  D_Flip_Flop d_ff_47 (.clk(clk), .D(c2), .Q(c3));  // open: Qn, preset, en, reset
  D_Flip_Flop d_ff_48 (.clk(clk), .D(c14), .Q(c15));  // open: Qn, preset, en, reset
  D_Flip_Flop d_ff_49 (.clk(clk), .D(c26), .Q(c27));  // open: Qn, preset, en, reset
  D_Flip_Flop d_ff_50 (.clk(clk), .D(and_5_out), .Q(estado2));  // open: Qn, preset, en, reset
  or or_33 (estado3, comparator_2_gt, comparator_3_lt);
  D_Flip_Flop d_ff_51 (.clk(clk), .D(and_6_out), .Q(estado1));  // open: Qn, preset, en, reset
  and and_6 (and_6_out, comparator_3_eq, o1p, o2p);
  or or_34 (_303, dx, s32, on, p2, p1);
  or or_35 (_313, dx, p2, on, s33, p1);
  D_Flip_Flop d_ff_52 (.clk(clk), .D(c3), .Q(c4));  // open: Qn, preset, en, reset
  D_Flip_Flop d_ff_53 (.clk(clk), .D(c15), .Q(c16));  // open: Qn, preset, en, reset
  D_Flip_Flop d_ff_54 (.clk(clk), .D(c27), .Q(c28), .Qn(d_ff_54_qn));  // open: preset, en, reset
  Keyboard #(.buflen(1)) keyboard_1 (.clk(clk), .data(keyboard_1_data));  // open: re, clr, avail
  D_Flip_Flop d_ff_55 (.clk(clk), .D(c4), .Q(c5), .Qn(d_ff_55_qn));  // open: preset, en, reset
  D_Flip_Flop d_ff_56 (.clk(clk), .D(c16), .Q(c17), .Qn(d_ff_56_qn));  // open: preset, en, reset
  D_Flip_Flop d_ff_57 (.clk(clk), .D(c28), .Q(c29));  // open: Qn, preset, en, reset
  or or_36 (_302, dx, s32, on, p1);
  or or_37 (_312, dx, s33, on, p1);
  D_Flip_Flop d_ff_58 (.clk(clk), .D(c5), .Q(c6));  // open: Qn, preset, en, reset
  D_Flip_Flop d_ff_59 (.clk(clk), .D(c17), .Q(c18));  // open: Qn, preset, en, reset
  D_Flip_Flop d_ff_60 (.clk(clk), .D(c29), .Q(c30));  // open: Qn, preset, en, reset
  not not_3 (not_3_out, k1);
  or or_38 (_301, s32, on, dx);
  or or_39 (_311, s33, on, dx);
  D_Flip_Flop d_ff_61 (.clk(clk), .D(c6), .Q(c7));  // open: Qn, preset, en, reset
  D_Flip_Flop d_ff_62 (.clk(clk), .D(c18), .Q(c19));  // open: Qn, preset, en, reset
  D_Flip_Flop d_ff_63 (.clk(clk), .D(c30), .Q(c31), .Qn(d_ff_63_qn));  // open: preset, en, reset
  iniciar iniciar_1 (.R(Iniciar), .not_Q(Ini));  // open: Q
  D_Flip_Flop d_ff_64 (.clk(clk), .D(and_7_out), .Q(d_ff_64_q), .preset(and_7_out), .reset(sw2));  // open: Qn, en
  and and_7 (and_7_out, agachar, not_3_out, dx);
  or or_40 (or_40_out, k3, q5);
  D_Flip_Flop d_ff_65 (.clk(clk), .D(c7), .Q(c8), .Qn(d_ff_65_qn));  // open: preset, en, reset
  D_Flip_Flop d_ff_66 (.clk(clk), .D(c19), .Q(c20), .Qn(d_ff_66_qn));  // open: preset, en, reset
  D_Flip_Flop d_ff_67 (.clk(clk), .D(c31), .Q(c32));  // open: Qn, preset, en, reset
  Comparator #(.width(7)) comparator_4 (.a(keyboard_1_data), .b(7'b1110011), .eq(agachar));  // open: gt, lt
  Comparator #(.width(7)) comparator_5 (.a(keyboard_1_data), .b(7'b1110111), .eq(saltar));  // open: gt, lt
  contador_Final contador (
    .Reset4(Iniciar), .Reset3(Iniciar), .Reset2(Iniciar), .Reset1(Iniciar), .conmutador(and_8_out),
    .gggg(ci7), .ffff(ci6), .eeee(ci5), .dddd(ci4), .cccc(ci3), .bbbb(ci2), .aaaa(ci1), .ggg(ce7), .fff(ce6),
    .eee(ce5), .ddd(ce4), .ccc(ce3), .bbb(ce2), .aaa(ce1), .gg(ca7), .ff(ca6), .ee(ca5), .dd(ca4), .cc(ca3),
    .bb(ca2), .aa(ca1), .g(co7), .f(co6), .e(co5), .d(co4), .c(co3), .b(co2), .a(co1));
  Demultiplexer #(.enable("false")) demultiplexer_9 (.out0(k1), .in(d_ff_64_q), .sel(dir3));  // open: out1
  Demultiplexer #(.enable("false")) demultiplexer_10 (.out0(k4), .out1(q4), .in(ch3), .sel(dir3));
  D_Flip_Flop d_ff_68 (.clk(clk), .D(or_40_out), .Q(ch3));  // open: Qn, preset, en, reset
  D_Flip_Flop d_ff_69 (.clk(clk), .D(c8), .Q(c9));  // open: Qn, preset, en, reset
  D_Flip_Flop d_ff_70 (.clk(clk), .D(c20), .Q(c21));  // open: Qn, preset, en, reset
  not not_4 (not_4_out, c32);
  not not_5 (not_5_out, s33);
  and and_8 (and_8_out, not_5_out, not_4_out);
  D_Flip_Flop d_ff_71 (.clk(clk), .D(c9), .Q(c10));  // open: Qn, preset, en, reset
  D_Flip_Flop d_ff_72 (.clk(clk), .D(c21), .Q(c22));  // open: Qn, preset, en, reset
  D_Flip_Flop d_ff_73 (.clk(clk), .D(or_41_out), .Q(ch1));  // open: Qn, preset, en, reset
  or or_41 (or_41_out, k1, q3);
  D_Flip_Flop d_ff_74 (.clk(clk), .D(or_42_out), .Q(ch4));  // open: Qn, preset, en, reset
  or or_42 (or_42_out, k4, in_3);
  Demultiplexer #(.enable("false")) demultiplexer_11 (.out0(k2), .out1(q2), .in(ch1), .sel(dir3));
  Demultiplexer #(.enable("false")) demultiplexer_12 (.out0(k5), .out1(q5), .in(ch4), .sel(dir3));
  D_Flip_Flop d_ff_75 (.clk(clk), .D(c10), .Q(c11), .Qn(d_ff_75_qn));  // open: preset, en, reset
  D_Flip_Flop d_ff_76 (.clk(clk), .D(c22), .Q(c23), .Qn(d_ff_76_qn));  // open: preset, en, reset
  D_Flip_Flop d_ff_77 (.clk(clk), .D(c11), .Q(c12));  // open: Qn, preset, en, reset
  D_Flip_Flop d_ff_78 (.clk(clk), .D(c23), .Q(c24));  // open: Qn, preset, en, reset
  Comparator #(.width(1)) comparator_6 (.a(q2), .b(ch1), .lt(sw2));  // open: gt, eq
  D_Flip_Flop d_ff_79 (.clk(clk), .D(or_43_out), .Q(ch2));  // open: Qn, preset, en, reset
  or or_43 (or_43_out, k2, q4);
  or or_44 (on, ch1, ch2, ch3, ch4);
  losing losing (
    .in_1(_301), .in_2(_311), .in_3(s31), .in_4(_305), .in_5(_301), .in_6(s31), .in_7(_311), .in_8(_315),
    .in_9(_311), .in_10(_301), .in_11(_306), .in_12(s31), .in_13(_315), .in_14(_301), .in_15(_311),
    .in_16(_316), .in_17(_315), .in_18(_305), .in_19(_301), .in_20(_311), .in_21(_306), .in_22(_316),
    .in_23(_305), .in_24(_315), .in_25(_3113), .in_26(_307), .in_27(c30), .in_28(_317), .in_29(_306),
    .in_30(_317), .in_31(_307), .out_32(fin));
  Demultiplexer #(.enable("false")) demultiplexer_13 (.out0(k3), .out1(q3), .in(ch2), .sel(dir3));
  nor nor_1 (o2p, s2, s3, s4, s5, s6, s7, s8, s9, s10, s11, s12, s13, s14);
  T_Flip_Flop t_ff_2 (.Q(dir3), .preset(ch4), .reset(sw2));  // open: clk, T, Qn, en
  nor nor_2 (o1p, c1, c2, c3, c4, c5, c6, c7, c8, c9, c10, c11, c12, c13);
  or or_45 (or_45_out, ch2, ch1, p1, p2, p3, p4, p5, p6, p7, ch3, ch4);
  not not_6 (dx, or_45_out);

  // Other names for the same wires on the sheet: dir = in_1

  // Notes on the sheet:
  //   Pantalla de Juego
  //   Presione "W" para saltar
  //   Presione "S" para agacharse
  //   Presione "Ctrl+R" para reiniciar el juego
  //   Presione "Ctrl+K" para pausar el juego o para Reanudar
  //   Nota: Si usted choca contra un obstaculo el juego se detendra y debera reiniciar para seguir jugando
  //   Puntos
  //   Tecla
endmodule

module contador_Parte_1 (
  input  Conmutador,
  input  reset,
  output sA,
  output sB,
  output sC,
  output sD,
  output vai1
);

  wire and_1_out, d_ff_1_q, d_ff_2_q, d_ff_3_q, d_ff_4_q;

  and and_1 (and_1_out, ~sA, sB, ~sC, sD);  // AND_Gate
  Multiplexer #(.enable("false")) multiplexer_1 (.in0(and_1_out), .in1(reset), .out(vai1), .sel(reset));
  D_Flip_Flop d_ff_1 (.clk(Conmutador), .D(sA), .Q(d_ff_1_q), .preset(vai1));  // open: Qn, en, reset
  D_Flip_Flop d_ff_2 (.clk(d_ff_1_q), .D(sB), .Q(d_ff_2_q), .preset(vai1));  // open: Qn, en, reset
  D_Flip_Flop d_ff_3 (.clk(d_ff_2_q), .D(sC), .Q(d_ff_3_q), .preset(vai1));  // open: Qn, en, reset
  D_Flip_Flop d_ff_4 (.clk(d_ff_3_q), .D(sD), .Q(d_ff_4_q), .preset(vai1));  // open: Qn, en, reset
  not not_1 (sA, d_ff_1_q);
  not not_2 (sB, d_ff_2_q);
  not not_3 (sC, d_ff_3_q);
  not not_4 (sD, d_ff_4_q);
endmodule

module contador_Parte_2 (
  input  clock,
  input  reset,
  output sA,
  output sB,
  output sC,
  output sD,
  output vai1
);

  wire and_1_out, d_ff_1_q, d_ff_2_q, d_ff_3_q, d_ff_4_q;

  and and_1 (and_1_out, ~sA, sB, ~sC, sD);  // AND_Gate
  Multiplexer #(.enable("false")) multiplexer_1 (.in0(and_1_out), .in1(reset), .out(vai1), .sel(reset));
  D_Flip_Flop d_ff_1 (.clk(clock), .D(sA), .Q(d_ff_1_q), .preset(vai1));  // open: Qn, en, reset
  D_Flip_Flop d_ff_2 (.clk(d_ff_1_q), .D(sB), .Q(d_ff_2_q), .preset(vai1));  // open: Qn, en, reset
  D_Flip_Flop d_ff_3 (.clk(d_ff_2_q), .D(sC), .Q(d_ff_3_q), .preset(vai1));  // open: Qn, en, reset
  D_Flip_Flop d_ff_4 (.clk(d_ff_3_q), .D(sD), .Q(d_ff_4_q), .preset(vai1));  // open: Qn, en, reset
  not not_1 (sA, d_ff_1_q);
  not not_2 (sB, d_ff_2_q);
  not not_3 (sC, d_ff_3_q);
  not not_4 (sD, d_ff_4_q);
endmodule

module contador_Parte_3 (
  input  clock,
  input  reset,
  output sA,
  output sB,
  output sC,
  output sD,
  output vai1
);

  wire and_1_out, d_ff_1_q, d_ff_2_q, d_ff_3_q, d_ff_4_q;

  and and_1 (and_1_out, ~sA, sB, sC, ~sD);  // AND_Gate
  D_Flip_Flop d_ff_1 (.clk(clock), .D(sA), .Q(d_ff_1_q), .preset(vai1));  // open: Qn, en, reset
  D_Flip_Flop d_ff_2 (.clk(d_ff_1_q), .D(sB), .Q(d_ff_2_q), .preset(vai1));  // open: Qn, en, reset
  D_Flip_Flop d_ff_3 (.clk(d_ff_2_q), .D(sC), .Q(d_ff_3_q), .preset(vai1));  // open: Qn, en, reset
  D_Flip_Flop d_ff_4 (.clk(d_ff_3_q), .D(sD), .Q(d_ff_4_q), .preset(vai1));  // open: Qn, en, reset
  Multiplexer #(.enable("false")) multiplexer_1 (.in0(and_1_out), .in1(reset), .out(vai1), .sel(reset));
  not not_1 (sA, d_ff_1_q);
  not not_2 (sB, d_ff_2_q);
  not not_3 (sC, d_ff_3_q);
  not not_4 (sD, d_ff_4_q);
endmodule

module contador_Parte_4 (
  input  [3:0] seletor,
  output a,
  output b,
  output c,
  output d,
  output e,
  output f,
  output g
);

  Multiplexer #(.select(4), .enable("false")) multiplexer_1 (
    .in0(1'b1), .in1(1'b0), .in2(1'b1), .in3(1'b1), .in4(1'b0), .in5(1'b1), .in6(1'b1), .in7(1'b1),
    .in8(1'b1), .in9(1'b1), .out(a), .sel(seletor));  // open: in10, in11, in12, in13, in14, in15
  Multiplexer #(.select(4), .enable("false")) multiplexer_2 (
    .in0(1'b1), .in1(1'b1), .in2(1'b0), .in3(1'b1), .in4(1'b1), .in5(1'b1), .in6(1'b1), .in7(1'b1),
    .in8(1'b1), .in9(1'b1), .out(c), .sel(seletor));  // open: in10, in11, in12, in13, in14, in15
  Multiplexer #(.select(4), .enable("false")) multiplexer_3 (
    .in0(1'b1), .in1(1'b0), .in2(1'b1), .in3(1'b0), .in4(1'b0), .in5(1'b0), .in6(1'b1), .in7(1'b0),
    .in8(1'b1), .in9(1'b0), .out(e), .sel(seletor));  // open: in10, in11, in12, in13, in14, in15
  Multiplexer #(.select(4), .enable("false")) multiplexer_4 (
    .in0(1'b0), .in1(1'b0), .in2(1'b1), .in3(1'b1), .in4(1'b1), .in5(1'b1), .in6(1'b1), .in7(1'b0),
    .in8(1'b1), .in9(1'b1), .in10(1'b0), .out(g), .sel(seletor));  // open: in11, in12, in13, in14, in15
  Multiplexer #(.select(4), .enable("false")) multiplexer_5 (
    .in0(1'b1), .in1(1'b1), .in2(1'b1), .in3(1'b1), .in4(1'b1), .in5(1'b0), .in6(1'b0), .in7(1'b1),
    .in8(1'b1), .in9(1'b1), .in10(1'b0), .out(b), .sel(seletor));  // open: in11, in12, in13, in14, in15
  Multiplexer #(.select(4), .enable("false")) multiplexer_6 (
    .in0(1'b1), .in1(1'b0), .in2(1'b1), .in3(1'b1), .in4(1'b0), .in5(1'b1), .in6(1'b1), .in7(1'b0),
    .in8(1'b1), .in9(1'b1), .in10(1'b1), .out(d), .sel(seletor));  // open: in11, in12, in13, in14, in15
  Multiplexer #(.select(4), .enable("false")) multiplexer_7 (
    .in0(1'b1), .in1(1'b0), .in2(1'b0), .in3(1'b0), .in4(1'b1), .in5(1'b1), .in6(1'b1), .in7(1'b0),
    .in8(1'b1), .in9(1'b1), .in10(1'b0), .out(f), .sel(seletor));  // open: in11, in12, in13, in14, in15
endmodule

module contador_Final (
  input  conmutador,
  input  Reset1,
  input  Reset4,
  input  Reset3,
  input  Reset2,
  output gggg,
  output eeee,
  output cccc,
  output aaaa,
  output ggg,
  output eee,
  output ccc,
  output aaa,
  output gg,
  output ee,
  output cc,
  output aa,
  output g,
  output e,
  output c,
  output a,
  output ffff,
  output dddd,
  output bbbb,
  output fff,
  output ddd,
  output bbb,
  output ff,
  output dd,
  output bb,
  output f,
  output d,
  output b
);

  wire contador_parte_1_1_vai1, contador_parte_2_1_vai1, contador_parte_3_2_vai1;
  wire [3:0] contador_parte_1_1_sa, contador_parte_2_1_sa, contador_parte_3_1_sa, contador_parte_3_2_sa;

  contador_Parte_3 contador_parte_3_1 (
    .clock(contador_parte_2_1_vai1), .reset(Reset4), .sA(contador_parte_3_1_sa[0]),
    .sB(contador_parte_3_1_sa[1]), .sC(contador_parte_3_1_sa[2]), .sD(contador_parte_3_1_sa[3]));  // open: vai1
  contador_Parte_2 contador_parte_2_1 (
    .clock(contador_parte_3_2_vai1), .reset(Reset3), .sA(contador_parte_2_1_sa[0]),
    .sB(contador_parte_2_1_sa[1]), .sC(contador_parte_2_1_sa[2]), .sD(contador_parte_2_1_sa[3]),
    .vai1(contador_parte_2_1_vai1));
  contador_Parte_4 contador_parte_4_1 (
    .seletor(contador_parte_3_1_sa), .a(aaaa), .b(bbbb), .c(cccc), .d(dddd), .e(eeee), .f(ffff), .g(gggg));
  contador_Parte_4 contador_parte_4_2 (
    .seletor(contador_parte_2_1_sa), .a(aaa), .b(bbb), .c(ccc), .d(ddd), .e(eee), .f(fff), .g(ggg));
  contador_Parte_3 contador_parte_3_2 (
    .clock(contador_parte_1_1_vai1), .reset(Reset2), .sA(contador_parte_3_2_sa[0]),
    .sB(contador_parte_3_2_sa[1]), .sC(contador_parte_3_2_sa[2]), .sD(contador_parte_3_2_sa[3]),
    .vai1(contador_parte_3_2_vai1));
  contador_Parte_1 contador_parte_1_1 (
    .Conmutador(conmutador), .reset(Reset1), .sA(contador_parte_1_1_sa[0]), .sB(contador_parte_1_1_sa[1]),
    .sC(contador_parte_1_1_sa[2]), .sD(contador_parte_1_1_sa[3]), .vai1(contador_parte_1_1_vai1));
  contador_Parte_4 contador_parte_4_3 (
    .seletor(contador_parte_3_2_sa), .a(aa), .b(bb), .c(cc), .d(dd), .e(ee), .f(ff), .g(gg));
  contador_Parte_4 contador_parte_4_4 (
    .seletor(contador_parte_1_1_sa), .a(a), .b(b), .c(c), .d(d), .e(e), .f(f), .g(g));
endmodule

module losing (
  input  in_1,
  input  in_2,
  input  in_3,
  input  in_4,
  input  in_5,
  input  in_6,
  input  in_7,
  input  in_8,
  input  in_9,
  input  in_10,
  input  in_11,
  input  in_12,
  input  in_13,
  input  in_14,
  input  in_15,
  input  in_16,
  input  in_17,
  input  in_18,
  input  in_19,
  input  in_20,
  input  in_21,
  input  in_22,
  input  in_23,
  input  in_24,
  input  in_25,
  input  in_26,
  input  in_27,
  input  in_28,
  input  in_29,
  input  in_30,
  input  in_31,
  output out_32
);

  wire and_1_out, and_2_out, and_3_out, and_4_out, and_5_out, and_6_out, and_7_out, not_1_out, not_2_out,
       not_3_out, not_4_out, not_5_out, not_6_out, not_7_out;

  and and_1 (and_1_out, in_1, in_2, in_3);
  not not_1 (not_1_out, in_5);
  and and_2 (and_2_out, in_4, not_1_out, in_6, not_2_out, in_8);
  not not_2 (not_2_out, in_7);
  not not_3 (not_3_out, in_9);
  and and_3 (and_3_out, not_3_out, in_10, in_11, in_12, not_4_out);
  not not_4 (not_4_out, in_13);
  not not_5 (not_5_out, in_14);
  and and_4 (and_4_out, not_5_out, in_15, in_16, in_17, not_6_out);
  not not_6 (not_6_out, in_18);
  and and_5 (and_5_out, in_19, in_20, in_21, in_22, in_23, in_24, in_25);
  and and_6 (and_6_out, in_26, in_27, in_28);
  not not_7 (not_7_out, in_30);
  and and_7 (and_7_out, in_29, not_7_out, in_31);
  or or_1 (out_32, and_1_out, and_2_out, and_3_out, and_4_out, and_5_out, and_6_out, and_7_out);
endmodule

module iniciar (
  input  R,
  output Q,
  output not_Q
);

  nor nor_1 (Q, R, not_Q);
  nor nor_2 (not_Q, Q, 1'b0);
endmodule
